# Fritzing sketch ART-shield (saved by Fritzing 0.4.3b)

parts:
  CPLD = DIP - 40 pins
  RFH2 = Generic female header - 9 pins [package=THT]
  RFH1 = Generic female header - 9 pins [package=THT]
  MH = Generic female header - 4 pins [package=THT]
  Arduino_Uno = Arduino
  RSV = Generic female header - 4 pins [package=THT]
  IR = Generic female header - 6 pins [package=THT]
  US = Generic female header - 10 pins [package=THT]

nets (from the pcb view):
  N1: CPLD.connector0, Arduino_Uno.D2
  N2: CPLD.connector1, Arduino_Uno.D3
  N3: CPLD.connector2, Arduino_Uno.D4
  N4: CPLD.connector3, Arduino_Uno.D5
  N5: CPLD.connector8, Arduino_Uno.D6
  N6: CPLD.connector9, Arduino_Uno.D7
  N7: CPLD.connector10, RSV.pin4
  N8: CPLD.connector11, RSV.pin3
  N9: CPLD.connector12, RSV.pin2
  N10: CPLD.connector13, RSV.pin1
  N11: CPLD.connector14, IR.pin1
  N12: CPLD.connector15, IR.pin2
  N13: CPLD.connector16, IR.pin3
  N14: CPLD.connector17, IR.pin4
  N15: CPLD.connector19, RFH2.pin1, Arduino_Uno.+5V, IR.pin6, US.pin10
  N16: CPLD.connector20, RFH1.pin1, Arduino_Uno.GND, IR.pin5, US.pin9
  N17: CPLD.connector21, MH.pin4
  N18: CPLD.connector22, MH.pin3
  N19: CPLD.connector23, MH.pin2
  N20: CPLD.connector24, MH.pin1
  N21: CPLD.connector27, US.pin8
  N22: CPLD.connector28, US.pin7
  N23: CPLD.connector29, US.pin6
  N24: CPLD.connector30, US.pin5
  N25: CPLD.connector31, US.pin4
  N26: CPLD.connector32, US.pin3
  N27: CPLD.connector33, US.pin2
  N28: CPLD.connector35, US.pin1
  N29: CPLD.connector36, Arduino_Uno.A0
  N30: CPLD.connector37, Arduino_Uno.A1
  N31: CPLD.connector38, Arduino_Uno.A2
  N32: CPLD.connector39, Arduino_Uno.A3
  N33: RFH2.pin3, Arduino_Uno.D11
  N34: RFH2.pin4, Arduino_Uno.D10
  N35: RFH1.pin4, Arduino_Uno.D12
  N36: RFH1.pin6, Arduino_Uno.D13
