# Fritzing sketch ART (saved by Fritzing 0.4.3b)

parts:
  Ultrasonic_Forward = SRF05 Ultrasonic Rangefinder
  IC1 = DIP - 40 pins
  RF_transceiver = RFC-1100A
  IF_Header = Generic female header - 3 pins [package=THT]
  UF_Header = Generic female header - 4 pins [package=THT]
  J4 = Generic female header - 9 pins [package=THT]
  J5 = Generic female header - 9 pins [package=THT]
  Infrared_Forward = Infrared Proximity Sensor
  Arduino1 = Arduino
  Ultrasonic_Right = SRF05 Ultrasonic Rangefinder
  IR_Header = Generic female header - 3 pins [package=THT]
  UR_Header = Generic female header - 4 pins [package=THT]
  Infrared_Right = Infrared Proximity Sensor
  J6 = Generic female header - 4 pins [package=THT]
  Ultrasonic_Backward = SRF05 Ultrasonic Rangefinder
  IB_Header = Generic female header - 3 pins [package=THT]
  UB_Header = Generic female header - 4 pins [package=THT]
  Infrared_Backward = Infrared Proximity Sensor
  Ultrasonic_Left = SRF05 Ultrasonic Rangefinder
  IL_Header = Generic female header - 3 pins [package=THT]
  UL_Header = Generic female header - 4 pins [package=THT]
  Infrared_Left = Infrared Proximity Sensor

nets:
  VCC: Ultrasonic_Forward.connector8, RF_transceiver.connector0, IF_Header.pin1, UF_Header.pin4, J4.pin9, J5.pin1, J5.pin2, Infrared_Forward.Vcc, Arduino1.+5V, Ultrasonic_Right.connector8, IR_Header.pin1, UR_Header.pin4, Infrared_Right.Vcc, Ultrasonic_Left.connector8, IL_Header.pin1, UL_Header.pin4, Infrared_Left.Vcc
  N1: Ultrasonic_Forward.connector9, IC1.connector36, UF_Header.pin3
  N2: Ultrasonic_Forward.connector10, IC1.connector35, UF_Header.pin2
  GND: Ultrasonic_Forward.connector11, RF_transceiver.connector17, IF_Header.pin2, UF_Header.pin1, J4.pin1, J4.pin2, Infrared_Forward.GND, Arduino1.GND, Ultrasonic_Right.connector11, IR_Header.pin2, UR_Header.pin1, Infrared_Right.GND, Ultrasonic_Left.connector11, IL_Header.pin2, UL_Header.pin1, Infrared_Left.GND
  N3: IC1.connector0, Arduino1.D2
  N4: IC1.connector1, Arduino1.D3
  N5: IC1.connector2, Arduino1.D4
  N6: IC1.connector3, Arduino1.D5
  N7: IC1.connector8, Arduino1.D6
  N8: IC1.connector9, Arduino1.D7
  N9: IC1.connector10, Ultrasonic_Left.connector9, UL_Header.pin3
  N10: IC1.connector11, Ultrasonic_Left.connector10, UL_Header.pin2
  N11: IC1.connector12, Arduino1.D8
  N12: IC1.connector13, Arduino1.D9
  N13: IC1.connector15, IL_Header.pin3, Infrared_Left.Vout
  N14: IC1.connector16, IB_Header.pin3, Infrared_Backward.Vout
  N15: IC1.connector21, J6.pin4
  N16: IC1.connector22, J6.pin3
  N17: IC1.connector23, J6.pin2
  N18: IC1.connector24, J6.pin1
  N19: IC1.connector25, Ultrasonic_Backward.connector9, UB_Header.pin3
  N20: IC1.connector26, Ultrasonic_Backward.connector10, UB_Header.pin2
  N21: IC1.connector27, IR_Header.pin3, Infrared_Right.Vout
  N22: IC1.connector31, Ultrasonic_Right.connector9, UR_Header.pin3
  N23: IC1.connector32, Ultrasonic_Right.connector10, UR_Header.pin2
  N24: IC1.connector33, IF_Header.pin3, Infrared_Forward.Vout
  N25: IC1.connector37, Arduino1.A1
  N26: IC1.connector38, Arduino1.A2
  N27: IC1.connector39, Arduino1.A3
  N28: RF_transceiver.connector3, J5.pin4, J5.pin5, Arduino1.D12
  N29: RF_transceiver.connector5, J5.pin6, J5.pin7, Arduino1.D13
  N30: RF_transceiver.connector14, J4.pin4, J4.pin5, Arduino1.D10
  N31: RF_transceiver.connector15, J4.pin3, Arduino1.D11
  N32: Ultrasonic_Backward.connector8, UB_Header.pin4
  N33: Ultrasonic_Backward.connector11, UB_Header.pin1
  N34: IB_Header.pin1, Infrared_Backward.Vcc
  N35: IB_Header.pin2, Infrared_Backward.GND
